// Logisim project SR.circ as structural Verilog: 1 circuit, main circuit main
module main (
  input  DS,
  input  PL,
  input  D0,
  input  D0_2,
  input  D0_3,
  input  D0_4,
  input  D0_5,
  input  D0_6,
  input  D0_7,
  input  D0_8,
  output Q,
  output Q_n
);

  wire and_1_out, and_2_out, and_3_out, and_4_out, and_5_out, and_6_out, and_7_out, and_8_out, and_9_out,
       and_10_out, and_11_out, and_12_out, and_13_out, and_14_out, and_15_out, and_16_out, clock_1_out,
       d_ff_1_q, d_ff_2_q, d_ff_3_q, d_ff_4_q, d_ff_5_q, d_ff_6_q, d_ff_7_q, not_1_out, not_2_out, not_3_out,
       not_4_out, not_5_out, not_6_out, not_7_out, not_8_out;

  Clock clock_1 (.out(clock_1_out));
  and and_1 (and_1_out, PL, D0);
  D_Flip_Flop d_ff_1 (.clk(clock_1_out), .D(DS), .Q(d_ff_1_q), .preset(and_1_out), .reset(and_2_out));  // open: Qn, en
  and and_2 (and_2_out, PL, not_1_out);
  not not_1 (not_1_out, D0);
  D_Flip_Flop d_ff_2 (
    .clk(clock_1_out), .D(d_ff_1_q), .Q(d_ff_2_q), .preset(and_4_out), .reset(and_3_out));  // open: Qn, en
  and and_3 (and_3_out, PL, not_2_out);
  and and_4 (and_4_out, PL, D0_2);
  not not_2 (not_2_out, D0_2);
  and and_5 (and_5_out, PL, D0_3);
  D_Flip_Flop d_ff_3 (
    .clk(clock_1_out), .D(d_ff_2_q), .Q(d_ff_3_q), .preset(and_5_out), .reset(and_6_out));  // open: Qn, en
  and and_6 (and_6_out, PL, not_3_out);
  not not_3 (not_3_out, D0_3);
  D_Flip_Flop d_ff_4 (
    .clk(clock_1_out), .D(d_ff_3_q), .Q(d_ff_4_q), .preset(and_7_out), .reset(and_8_out));  // open: Qn, en
  and and_7 (and_7_out, PL, D0_4);
  and and_8 (and_8_out, PL, not_4_out);
  not not_4 (not_4_out, D0_4);
  and and_9 (and_9_out, PL, D0_5);
  D_Flip_Flop d_ff_5 (
    .clk(clock_1_out), .D(d_ff_4_q), .Q(d_ff_5_q), .preset(and_9_out), .reset(and_10_out));  // open: Qn, en
  and and_10 (and_10_out, PL, not_5_out);
  not not_5 (not_5_out, D0_5);
  D_Flip_Flop d_ff_6 (
    .clk(clock_1_out), .D(d_ff_5_q), .Q(d_ff_6_q), .preset(and_12_out), .reset(and_11_out));  // open: Qn, en
  and and_11 (and_11_out, PL, not_6_out);
  and and_12 (and_12_out, PL, D0_6);
  not not_6 (not_6_out, D0_6);
  and and_13 (and_13_out, PL, D0_7);
  D_Flip_Flop d_ff_7 (
    .clk(clock_1_out), .D(d_ff_6_q), .Q(d_ff_7_q), .preset(and_13_out), .reset(and_14_out));  // open: Qn, en
  and and_14 (and_14_out, PL, not_7_out);
  not not_7 (not_7_out, D0_7);
  D_Flip_Flop d_ff_8 (
    .clk(clock_1_out), .D(d_ff_7_q), .Q(Q), .Qn(Q_n), .preset(and_16_out), .reset(and_15_out));  // open: en
  and and_15 (and_15_out, PL, not_8_out);
  and and_16 (and_16_out, PL, D0_8);
  not not_8 (not_8_out, D0_8);
endmodule
